# Fritzing sketch sketch (saved by Fritzing 0.9.6b)

parts:
  M1 = BME280
  Part1 = Adafruit 1.54" Tri-Color eInk / ePaper Display with SRAM [part_number=3625]
  M2 = ESP32-C3-DevKitM-1 [part_number=ESP32-C3-DevKitM-1]

nets:
  VIN: M1.VIN, Part1.VIN, M2.3V3-17, M2.3V3-18
  GND: M1.GND, Part1.GND, M2.GND-1, M2.GND-16, M2.GND-30
  N1: M1.SCL, M2.2
  N2: M1.SDA, M2.1
  N3: Part1.SCLK, M2.6
  N4: Part1.MISO, M2.7
  N5: Part1.DISPCS, M2.8
  N6: Part1.DC, M2.19
  N7: Part1.RESET, M2.10
  N8: Part1.BUSY, M2.9

custom parts:
  BME280: Temperature Humidity Barometric presure Sensor
  Adafruit 1.54" Tri-Color eInk / ePaper Display with SRAM: This small 1.54" tri-color display has 152x152 black and red ink pixels and a white-ish background. Using our Arduino library, you can create a 'frame buffer' with what pixels you want to have activated and then write that out to the display. We tossed a small SRAM chip on the back. This chip shares the SPI port the eInk display uses, so you only need one extra pin. And, no more frame-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
  ESP32-C3-DevKitM-1: Espressif Esp32 DevKit v1 is one of the development board created by DOIT to evaluate the ESP-WROOM-32 module. It is based on the ESP32 microcontroller that boasts Wifi, Bluetooth, Ethernet and Low Power support all in a single chip. (vanepp) Feb 2021: converted to ESP32-C3-DevKitM-1. This chip is 30pins long (2 x15) and 11 pins width.
